// Digital circuit part_c.dig as structural Verilog
module part_c (
  input  in_1,
  input  in_2,
  input  in_0,
  output out_0
);

  wire fgnfet_1_d, fgpfet_1_d;

  FGNFET fgnfet_1 (.G(in_1), .D(fgnfet_1_d), .S(out_0));
  FGPFET fgpfet_1 (.G(in_1), .S(out_0), .D(fgpfet_1_d));
  FGPFET fgpfet_2 (.G(in_2), .S(fgpfet_1_d), .D(1'b0));
  FGNFET fgnfet_2 (.G(in_0), .D(1'b1), .S(fgnfet_1_d));
  FGNFET fgnfet_3 (.G(in_2), .D(fgnfet_1_d), .S(out_0));
  FGPFET fgpfet_3 (.G(in_0), .S(out_0), .D(1'b0));
endmodule

/* Test case part_c_test:
in_0 in_1 in_2 out_0
0     0    0    0
0     0    1    0
0     1    0    0
0     1    1    0
1     0    0    0
1     0    1    1
1     1    0    1
1     1    1    1
*/
